// Logisim project lab 5.circ as structural Verilog: 7 circuits, main circuit main
module main (
  output [7:0] out_1,
  output [7:0] out_2
);

  AddMachine addmachine_1 (.out_1(out_1), .out_2(out_2));
endmodule

module NAND (
  input  in_1,
  input  in_2,
  output out_3
);

  wire and_1_out;

  and and_1 (and_1_out, in_1, in_2);
  not not_1 (out_3, and_1_out);
endmodule

module NOR (
  input  in_1,
  input  in_2,
  output out_3
);

  wire or_1_out;

  or or_1 (or_1_out, in_1, in_2);
  not not_1 (out_3, or_1_out);
endmodule

module XOR (
  input  in_1,
  input  in_2,
  output out_3
);

  wire and_1_out, not_1_out, or_1_out;

  and and_1 (and_1_out, in_1, in_2, in_2);
  not not_1 (not_1_out, and_1_out);
  or or_1 (or_1_out, in_2, in_1);
  and and_2 (out_3, not_1_out, or_1_out);
endmodule

module _2_to_1_MUX (
  input  Input_1,
  input  Select,
  input  Input_2,
  output out_4
);

  wire and_1_out, and_2_out, not_1_out;

  not not_1 (not_1_out, Select);
  and and_1 (and_1_out, Input_1, not_1_out);
  and and_2 (and_2_out, Select, Input_2);
  or or_1 (out_4, and_1_out, and_1_out, and_2_out, and_2_out);
endmodule

module _4_to_1_MUX (
  input  Select_1,
  input  Select_2,
  input  Input_1,
  input  Input_2,
  input  Input_3,
  input  Input_4,
  output out_7
);

  wire and_1_out, and_2_out, and_3_out, and_4_out, not_1_out, not_2_out;

  not not_1 (not_1_out, Select_1);
  not not_2 (not_2_out, Select_2);
  and and_1 (and_1_out, Input_1, not_2_out, not_1_out);
  and and_2 (and_2_out, Input_2, not_2_out, Select_1);
  and and_3 (and_3_out, Input_3, Select_2, not_1_out);
  and and_4 (and_4_out, Input_4, Select_2, Select_1);
  or or_1 (out_7, and_1_out, and_2_out, and_3_out, and_4_out);
endmodule

module AddMachine (
  output [7:0] out_1,
  output [7:0] out_2
);

  wire clock_1_out;

  Adder adder_1 (.a(out_1), .b(8'h1), .out(out_2));  // open: cin, cout
  Register register_1 (.D(out_2), .Q(out_1), .clk(clock_1_out));  // open: en, clr
  Clock clock_1 (.out(clock_1_out));
endmodule
