// Logisim project alu.circ as structural Verilog: 1 circuit, main circuit main
module main (
  input  [31:0] X,
  input  [31:0] Y,
  input  [3:0] Switch,
  output Signed_Overflow,
  output Equal,
  output [31:0] Result,
  output [31:0] Result_2
);

  wire comparator_1_lt, comparator_2_lt, overadd, oversub, xnor_1_out, xor_2_out, xor_3_out, xor_4_out;
  wire [4:0] Xtrunc;
  wire [31:0] add, \and , divrem, divu, mult, multup, \nor , \or , sll, slt, sltu, sra, srl, sub, \xor ;

  Multiplexer #(.select(4), .width(32)) multiplexer_1 (
    .in0({32{1'b0}}), .in1({32{1'b0}}), .in2({32{1'b0}}), .in3(multup), .in4(divrem), .in5({32{1'b0}}),
    .in6({32{1'b0}}), .in7({32{1'b0}}), .in8({32{1'b0}}), .in9({32{1'b0}}), .in10({32{1'b0}}),
    .in11({32{1'b0}}), .in12({32{1'b0}}), .in13({32{1'b0}}), .in14({32{1'b0}}), .in15({32{1'b0}}),
    .out(Result_2), .sel(Switch));  // open: en
  Multiplexer #(.select(4), .width(32)) multiplexer_2 (
    .in0(sll), .in1(srl), .in2(sra), .in3(mult), .in4(divu), .in5(add), .in6(add), .in7(sub), .in8(sub),
    .in9(\and ), .in10(\or ), .in11(\xor ), .in12(\nor ), .in13(slt), .in14(sltu), .in15({32{1'b0}}),
    .out(Result), .sel(Switch));  // open: en
  Bit_Extender #(.in_width(32), .out_width(5)) bit_extender_1 (.in(X), .out(Xtrunc));
  assign \and  = X & Y;  // AND_Gate and_1, 32 bits wide
  Adder #(.width(32)) adder_1 (.a(X), .b(Y), .out(add));  // open: cin, cout
  Multiplier #(.width(32)) multiplier_1 (.a(X), .b(Y), .out(mult), .cout(multup));  // open: cin
  assign \or  = X | Y;  // OR_Gate or_1, 32 bits wide
  Divider #(.width(32)) divider_1 (.a(X), .b(Y), .out(divu), .rem(divrem));  // open: upper
  Shifter #(.width(32)) shifter_1 (.in(Y), .\dist (Xtrunc), .out(sll));
  Multiplexer #(.select(4)) multiplexer_3 (
    .in0(1'b0), .in1(1'b0), .in2(1'b0), .in3(1'b0), .in4(1'b0), .in5(overadd), .in6(1'b0), .in7(oversub),
    .in8(1'b0), .in9(1'b0), .in10(1'b0), .in11(1'b0), .in12(1'b0), .in13(1'b0), .in14(1'b0), .in15(1'b0),
    .out(Signed_Overflow), .sel(Switch));  // open: en
  assign \xor  = X ^ Y;  // XOR_Gate xor_1, 32 bits wide
  Shifter #(.width(32), .shift("lr")) shifter_2 (.in(Y), .\dist (Xtrunc), .out(srl));
  assign \nor  = ~(X | Y);  // NOR_Gate nor_1, 32 bits wide
  Subtractor #(.width(32)) subtractor_1 (.a(X), .b(Y), .out(sub));  // open: bin, bout
  Comparator #(.width(32)) comparator_1 (.a(X), .b(Y), .eq(Equal), .lt(comparator_1_lt));  // open: gt
  assign slt = {{31{1'b0}}, comparator_1_lt};  // Bit_Extender bit_extender_2
  Comparator #(.width(32), .mode("unsigned")) comparator_2 (.a(X), .b(Y), .lt(comparator_2_lt));  // open: gt, eq
  Shifter #(.width(32), .shift("ar")) shifter_3 (.in(Y), .\dist (Xtrunc), .out(sra));
  xor xor_2 (xor_2_out, sub[31], X[31]);
  xor xor_3 (xor_3_out, X[31], Y[31]);
  assign sltu = {{31{1'b0}}, comparator_2_lt};  // Bit_Extender bit_extender_3
  xor xor_4 (xor_4_out, add[31], X[31]);
  xnor xnor_1 (xnor_1_out, X[31], Y[31]);
  and and_2 (oversub, xor_2_out, xor_3_out);
  and and_3 (overadd, xor_4_out, xnor_1_out);

  // Other names for the same wires on the sheet: overflow = Signed_Overflow; S[3:0] = Switch

  // Notes on the sheet:
  //   INPUTS to your circuit
  //   OUTPUTS from your circuit
endmodule
