// Logisim project cpu.circ as structural Verilog: 3 circuits, main circuit main
module main (
  input  [31:0] INSTRUCTION,
  input  CLOCK,
  output [31:0] FETCH_ADDRESS,
  output [31:0] s0_Value,
  output [31:0] s1_Value,
  output [31:0] s2_Value,
  output [31:0] ra_Value,
  output [31:0] sp_Value,
  output [31:0] HI_Value,
  output [31:0] LO_Value
);

  wire ALUSrc, and_1_out, and_2_out, beqinc, beqincon, Branch, branchtrue, Divu, Jump, JumpReg, Lui,
       main_2_equal, main_2_signed_overflow, MEM_p1, MEM_p2, MEM_p4, MEM_p10, MEM_p13, MEM_p16, MemRead,
       MemToReg, MemWrite, Mfhi, Mflo, Mult, not_1_out, not_2_out, NotBranch, or_3_out, RAChange, RegDst,
       RegWrite, RegWriteTrue, ShiftOn, Stall, ZeroExtend;
  wire [3:0] alucontroller_1_aluswitch;
  wire [4:0] multiplexer_2_out, multiplexer_3_out, Read1, Read2;
  wire [5:0] Opcode;
  wire [15:0] Imm;
  wire [31:0] adder_1_out, adder_2_out, beqincdata, bit_extender_2_out, bit_extender_3_out, LuiData,
       main_1_read_data_2, MEM_p11, MEM_p15, multiplexer_1_out, multiplexer_4_out, multiplexer_5_out,
       multiplexer_6_out, multiplexer_7_out, multiplexer_8_out, multiplexer_9_out, multiplexer_10_out,
       multiplexer_11_out, multiplexer_13_out, NextAddr, RegAddr, Result, Result2, Shift, shifter_2_out,
       WriteData;

  Controller controller_1 (
    .opcode(Opcode), .RegDst(RegDst), .ALUSrc(ALUSrc), .MemToReg(MemToReg), .RegWrite(RegWrite),
    .MemRead(MemRead), .MemWrite(MemWrite), .Branch(Branch), .NotBranch(NotBranch), .Jump(Jump));
  assign Shift = {{27{1'b0}}, Imm[10:6]};  // Bit_Extender bit_extender_1
  or or_1 (RegWriteTrue, RegWrite, beqincon);
  Multiplexer #(.width(32)) multiplexer_1 (
    .in0(INSTRUCTION), .in1({32{1'b0}}), .out(multiplexer_1_out), .sel(Stall));  // open: en
  or or_2 (Stall, Jump, JumpReg, branchtrue);
  or or_3 (or_3_out, Divu, Mult);
  Register #(.width(32)) PC (.D(NextAddr), .en(1'b1), .Q(FETCH_ADDRESS), .clk(CLOCK));  // open: clr
  Register #(.width(32)) register_1 (
    .D(multiplexer_1_out), .en(1'b1), .Q({Opcode, Read1, Read2, Imm}), .clk(CLOCK));  // open: clr
  Register #(.width(32)) HI (.D(Result2), .en(or_3_out), .Q(HI_Value), .clk(CLOCK));  // open: clr
  Register #(.width(32)) LO (.D(Result), .en(or_3_out), .Q(LO_Value), .clk(CLOCK));  // open: clr
  Multiplexer #(.width(5)) multiplexer_2 (
    .in0(Read2), .in1(Imm[15:11]), .out(multiplexer_2_out), .sel(RegDst));  // open: en
  Multiplexer #(.width(5)) multiplexer_3 (
    .in0(multiplexer_2_out), .in1({5{1'b1}}), .out(multiplexer_3_out), .sel(RAChange));  // open: en
  Multiplexer #(.width(32)) multiplexer_4 (
    .in0(WriteData), .in1(FETCH_ADDRESS), .out(multiplexer_4_out), .sel(RAChange));  // open: en
  assign bit_extender_2_out = {{16{Imm[15]}}, Imm};  // Bit_Extender bit_extender_2
  assign bit_extender_3_out = {{16{1'b0}}, Imm};  // Bit_Extender bit_extender_3
  Adder #(.width(32)) adder_1 (.a(FETCH_ADDRESS), .b(32'h4), .out(adder_1_out));  // open: cin, cout
  regfile_main main_1 (
    .Read_Register_1(Read1), .Read_Register_2(Read2), .Write_Register(multiplexer_3_out),
    .Write_Data(multiplexer_5_out), .Write_Enable(RegWriteTrue), .Clock(CLOCK), .Read_Data_1(RegAddr),
    .Read_Data_2(main_1_read_data_2), .s0_Value(s0_Value), .s1_Value(s1_Value), .s2_Value(s2_Value),
    .ra_Value(ra_Value), .sp_Value(sp_Value));
  Multiplexer #(.width(32)) multiplexer_5 (
    .in0(multiplexer_6_out), .in1(LO_Value), .out(multiplexer_5_out), .sel(Mflo));  // open: en
  Multiplexer #(.width(32)) multiplexer_6 (
    .in0(multiplexer_4_out), .in1(HI_Value), .out(multiplexer_6_out), .sel(Mfhi));  // open: en
  Multiplexer #(.width(32)) multiplexer_7 (
    .in0(bit_extender_2_out), .in1(bit_extender_3_out), .out(multiplexer_7_out), .sel(ZeroExtend));  // open: en
  Shifter #(.width(32)) shifter_1 (.in(bit_extender_3_out), .\dist (5'b10000), .out(LuiData));
  Shifter #(.width(32)) shifter_2 (.in(multiplexer_7_out), .\dist (5'b00010), .out(shifter_2_out));
  alucontroller alucontroller_1 (
    .ALUSwitch(alucontroller_1_aluswitch), .Opcode(Opcode), .Funct(Imm[5:0]), .BeqInc(beqinc), .Lui(Lui),
    .JumpReg(JumpReg), .ZeroExtend(ZeroExtend), .RAChange(RAChange), .Mfhi(Mfhi), .Mflo(Mflo), .Mult(Mult),
    .Divu(Divu), .Shift(ShiftOn));
  Adder #(.width(32)) adder_2 (.a(FETCH_ADDRESS), .b(shifter_2_out), .out(adder_2_out));  // open: cin, cout
  LED led_1 (.in(main_2_signed_overflow));
  Multiplexer #(.width(32)) multiplexer_8 (
    .in0(RegAddr), .in1(Shift), .out(multiplexer_8_out), .sel(ShiftOn));  // open: en
  Multiplexer #(.width(32)) multiplexer_9 (
    .in0(main_1_read_data_2), .in1(multiplexer_7_out), .out(multiplexer_9_out), .sel(ALUSrc));  // open: en
  alu_main main_2 (
    .Switch(alucontroller_1_aluswitch), .X(multiplexer_8_out), .Equal(main_2_equal), .Result(Result),
    .Signed_Overflow(main_2_signed_overflow), .Y(multiplexer_9_out), .Result_2(Result2));
  Multiplexer #(.width(32)) multiplexer_10 (
    .in0(adder_1_out), .in1(adder_2_out), .out(multiplexer_10_out), .sel(branchtrue));  // open: en
  or or_4 (branchtrue, and_1_out, and_2_out);
  and and_1 (and_1_out, Branch, main_2_equal);
  Adder #(.width(32)) adder_3 (.a(multiplexer_9_out), .b(32'h1), .out(beqincdata));  // open: cin, cout
  Multiplexer #(.width(32)) multiplexer_11 (
    .in0(multiplexer_10_out), .in1({adder_1_out[31:28], INSTRUCTION[25:0], 2'b00}), .out(multiplexer_11_out),
    .sel(Jump));  // open: en
  and and_2 (and_2_out, not_1_out, NotBranch);
  not not_1 (not_1_out, main_2_equal);
  // mem_main MEM: pin names not known; wires that end beside it: MEM_p1, MEM_p2, MEM_p2, MEM_p4, Result, main_1_read_data_2, MemWrite, MEM_p4, CLOCK, MEM_p10, MEM_p11, MEM_p10, MEM_p13, MEM_p13, MEM_p15, MEM_p16, MEM_p16
  Multiplexer #(.width(32)) multiplexer_12 (
    .in0(multiplexer_11_out), .in1(RegAddr), .out(NextAddr), .sel(JumpReg));  // open: en
  not not_2 (not_2_out, branchtrue);
  Multiplexer #(.width(32)) multiplexer_13 (
    .in0(Result), .in1(MEM_p11), .out(multiplexer_13_out), .sel(MemRead));  // open: en
  and and_3 (beqincon, not_2_out, beqinc);
  Multiplexer #(.width(32)) multiplexer_14 (
    .in0(multiplexer_13_out), .in1(LuiData), .out(MEM_p15), .sel(Lui));  // open: en
  Multiplexer #(.width(32)) multiplexer_15 (
    .in0(MEM_p15), .in1(beqincdata), .out(WriteData), .sel(beqincon));  // open: en

  // Other names for the same wires on the sheet: JumpAddress[25:0] = INSTRUCTION[25:0]; clk = CLOCK;
  //   fetch_addr[31:0] = FETCH_ADDRESS; PC4[31:0] = FETCH_ADDRESS; hi_val[31:0] = HI_Value; lo_val[31:0] = LO_Value;
  //   ra_val[31:0] = ra_Value; s0_val[31:0] = s0_Value; s1_val[31:0] = s1_Value; s2_val[31:0] = s2_Value;
  //   sp_val[31:0] = sp_Value

  // Notes on the sheet:
  //   Output
  //   These are outputs/inputs from run.circ
  //   Inputs
  //   These are DEBUG/TEST outputs from your circuit.
endmodule

module Controller (
  input  [5:0] opcode,
  output RegDst,
  output ALUSrc,
  output MemToReg,
  output RegWrite,
  output MemRead,
  output MemWrite,
  output Branch,
  output NotBranch,
  output Jump
);

  wire BEQ_out, BEQINC_out, J_out, JAL_out, or_1_out, or_2_out;

  and Rtype (RegDst, ~opcode[0], ~opcode[1], ~opcode[2], ~opcode[3], ~opcode[4], ~opcode[5]);  // AND_Gate
  and LW (MemRead, opcode[0], opcode[1], ~opcode[2], ~opcode[3], ~opcode[4], opcode[5]);  // AND_Gate
  and SW (MemWrite, opcode[0], opcode[1], ~opcode[2], opcode[3], ~opcode[4], opcode[5]);  // AND_Gate
  and BEQ (BEQ_out, ~opcode[0], ~opcode[1], opcode[2], ~opcode[3], ~opcode[4], ~opcode[5]);  // AND_Gate
  and BNE (NotBranch, opcode[0], ~opcode[1], opcode[2], ~opcode[3], ~opcode[4], ~opcode[5]);  // AND_Gate
  and J (J_out, ~opcode[0], opcode[1], ~opcode[2], ~opcode[3], ~opcode[4], ~opcode[5]);  // AND_Gate
  and JAL (JAL_out, opcode[0], opcode[1], ~opcode[2], ~opcode[3], ~opcode[4], ~opcode[5]);  // AND_Gate
  and BEQINC (BEQINC_out, ~opcode[0], opcode[1], opcode[2], ~opcode[3], ~opcode[4], ~opcode[5]);  // AND_Gate
  not not_1 (ALUSrc, or_1_out);
  or or_1 (or_1_out, BEQINC_out, NotBranch, BEQ_out, RegDst);
  or or_2 (or_2_out, BEQ_out, MemWrite, J_out, BEQINC_out, NotBranch);
  not not_2 (RegWrite, or_2_out);
  or or_3 (Branch, BEQINC_out, BEQ_out);
  or or_4 (Jump, J_out, JAL_out);

  assign MemToReg = MemRead;
endmodule

module alucontroller (
  input  [5:0] Opcode,
  input  [5:0] Funct,
  output [3:0] ALUSwitch,
  output Lui,
  output Mult,
  output BeqInc,
  output Divu,
  output RAChange,
  output Shift,
  output JumpReg,
  output Mfhi,
  output ZeroExtend,
  output Mflo
);

  wire decoder_3_out4, decoder_3_out5, EqualOpcode, fadd10, faddu10, fand10, fjalr00, fjr00, fnor10, for10,
       fsll00, fslt10, fsltu10, fsra00, fsrl00, fsub10, fsubu10, fxor10, GreaterOpcode, lwadd, not_1_out,
       not_2_out, not_3_out, not_4_out, not_5_out, not_6_out, not_7_out, not_8_out, not_9_out, not_10_out,
       oadd00, oaddu00, oand00, oj00, ojal00, oor00, or_1_out, or_2_out, or_3_out, or_4_out, oslt00, osltu00,
       osub00, oxor00, swadd;
  wire [11:5] or_8_out;

  not not_1 (not_1_out, EqualOpcode);
  not not_2 (not_2_out, EqualOpcode);
  Comparator #(.width(6)) comparator_1 (.a(6'b101011), .b(Opcode), .eq(swadd));  // open: gt, lt
  Decoder #(.select(4), .disabled(0)) decoder_1 (
    .out0(fsll00), .out2(fsrl00), .out3(fsra00), .out8(fjr00), .out9(fjalr00), .sel(Funct[3:0]),
    .en(not_3_out));  // open: out1, out4, out5, out6, out7, out10, out11, out12, out13, out14, out15
  not not_3 (not_3_out, or_1_out);
  or or_1 (or_1_out, not_1_out, Funct[5], Funct[4]);
  Decoder #(.select(4), .disabled(0)) decoder_2 (
    .out0(fadd10), .out1(faddu10), .out2(fsub10), .out3(fsubu10), .out4(fand10), .out5(for10), .out6(fxor10),
    .out7(fnor10), .out10(fslt10), .out11(fsltu10), .sel(Funct[3:0]), .en(not_4_out));  // open: out8, out9, out12, out13, out14, out15
  or or_2 (or_2_out, not_2_out, not_5_out, Funct[4]);
  not not_4 (not_4_out, or_2_out);
  not not_5 (not_5_out, Funct[5]);
  Comparator #(.width(6)) comparator_2 (.a(6'b100011), .b(Opcode), .eq(lwadd));  // open: gt, lt
  not not_6 (not_6_out, GreaterOpcode);
  Decoder #(.select(4), .disabled(0)) decoder_3 (
    .out2(oj00), .out3(ojal00), .out4(decoder_3_out4), .out5(decoder_3_out5), .out6(BeqInc), .out8(oadd00),
    .out9(oaddu00), .out10(oslt00), .out11(osltu00), .out12(oand00), .out13(oor00), .out14(oxor00),
    .out15(Lui), .sel(Opcode[3:0]), .en(not_7_out));  // open: out0, out1, out7
  or or_3 (or_3_out, not_6_out, Opcode[5], Opcode[4]);
  not not_7 (not_7_out, or_3_out);
  not not_8 (not_8_out, EqualOpcode);
  or or_4 (or_4_out, not_8_out, Funct[5], not_9_out);
  not not_9 (not_9_out, Funct[4]);
  or or_5 (JumpReg, fjalr00, fjr00);
  or or_6 (ZeroExtend, oand00, oxor00, oor00);
  Comparator #(.width(6), .mode("unsigned")) comparator_3 (
    .a(Opcode), .b({6{1'b0}}), .gt(GreaterOpcode), .eq(EqualOpcode));  // open: lt
  or or_7 (osub00, decoder_3_out4, decoder_3_out5);
  Decoder #(.select(4), .disabled(0)) decoder_4 (
    .out0(Mfhi), .out2(Mflo), .out8(Mult), .out11(Divu), .sel(Funct[3:0]), .en(not_10_out));  // open: out1, out3, out4, out5, out6, out7, out9, out10, out12, out13, out14, out15
  not not_10 (not_10_out, or_4_out);
  or or_8 (or_8_out[5], fadd10, oadd00, swadd, lwadd);
  or or_9 (or_8_out[6], faddu10, oaddu00);
  or or_10 (or_8_out[7], fsub10, BeqInc, osub00);
  or or_11 (or_8_out[9], fand10, oand00);
  or or_12 (or_8_out[10], for10, oor00);
  or or_13 (or_8_out[11], fxor10, oxor00);
  or or_14 (RAChange, fjalr00, ojal00);
  or or_15 (Shift, fsll00, fsrl00, fsra00);
  BitFinder #(.width(16), .\type ("high1")) bitfinder_1 (
    .in({1'b0, fsltu10, fslt10, fnor10, or_8_out[11:9], fsubu10, or_8_out[7:5], Divu, Mult, fsra00, fsrl00, fsll00}),
    .index(ALUSwitch));  // open: found

  // Other names for the same wires on the sheet: fmul01 = Mult; fdivu01 = Divu; fmfhi01 = Mfhi; fmflo01 = Mflo;
  //   FunctSelect[3:0] = Funct[3:0]; _5thFunct = Funct[4]; _6thFunct = Funct[5]; obeqinc00 = BeqInc; olui00 = Lui;
  //   OpcodeSelect[3:0] = Opcode[3:0]; _5thOpcode = Opcode[4]; _6thOpcode = Opcode[5]

  // Notes on the sheet:
  //   Funct With 00 (Top Middle)
  //   Funct With 10 (Middle-Lower Middle)
  //   Opcode With 00 (Top Left)
  //   Funct With 01 (Middle Middle)
endmodule
