// Logisim project regfile.circ as structural Verilog: 1 circuit, main circuit main
module main (
  input  [4:0] Read_Register_1,
  input  [4:0] Read_Register_2,
  input  [4:0] Write_Register,
  input  [31:0] Write_Data,
  input  Write_Enable,
  input  Clock,
  output [31:0] s0_Value,
  output [31:0] s1_Value,
  output [31:0] s2_Value,
  output [31:0] ra_Value,
  output [31:0] sp_Value,
  output [31:0] Read_Data_1,
  output [31:0] Read_Data_2
);

  wire _0_en, _1_en, _2_en, _3_en, _4_en, _5_en, _6_en, _7_en, _8_en, _9_en, _10_en, _11_en, _12_en, _13_en,
       _14_en, _15_en, _16_en, _17_en, _18_en, _19_en, _20_en, _21en, _22_en, _23_en, _24_en, _25_en, _26_en,
       _27_en, _28_en, _29_en, _30_en, _31_en, and_1_out, and_2_out, and_3_out, and_4_out, and_5_out,
       and_6_out, and_7_out, and_8_out, and_9_out, and_10_out, and_11_out, and_12_out, and_13_out,
       and_14_out, and_15_out, and_16_out, and_17_out, and_18_out, and_19_out, and_20_out, and_21_out,
       and_22_out, and_23_out, and_24_out, and_25_out, and_26_out, and_27_out, and_28_out, and_29_out,
       and_30_out, and_31_out;
  wire [31:0] _0_in, _0_out, _1_in, _1_out, _2_in, _2_out, _3_in, _3_out, _4_in, _4_out, _5_in, _5_out,
       _6_in, _6_out, _7_in, _7_out, _8_in, _8_out, _9_in, _9_out, _10_in, _10_out, _11_in, _11_out, _12_in,
       _12_out, _13_in, _13_out, _14_in, _14_out, _15_in, _15_out, _16_in, _17_in, _18_in, _19_in, _19_out,
       _20_in, _20_out, _21_in, _21_out, _22_in, _22_out, _23_in, _23_out, _24_in, _24_out, _25_in, _25_out,
       _26_in, _26_out, _27_in, _27_out, _28_in, _28_out, _29_in, _30_in, _30_out, _31_in;

  Demultiplexer #(.select(5), .width(32)) demultiplexer_1 (
    .out0(_0_in), .out1(_1_in), .out2(_2_in), .out3(_3_in), .out4(_4_in), .out5(_5_in), .out6(_6_in),
    .out7(_7_in), .out8(_8_in), .out9(_9_in), .out10(_10_in), .out11(_11_in), .out12(_12_in), .out13(_13_in),
    .out14(_14_in), .out15(_15_in), .out16(_16_in), .out17(_17_in), .out18(_18_in), .out19(_19_in),
    .out20(_20_in), .out21(_21_in), .out22(_22_in), .out23(_23_in), .out24(_24_in), .out25(_25_in),
    .out26(_26_in), .out27(_27_in), .out28(_28_in), .out29(_29_in), .out30(_30_in), .out31(_31_in),
    .in(Write_Data), .sel(Write_Register));  // open: en
  Register #(.width(32)) _0 (.D(_0_in), .en(1'b0), .Q(_0_out), .clk(Clock));  // open: clr
  Register #(.width(32)) _2 (.D(_2_in), .en(and_1_out), .Q(_2_out), .clk(Clock));  // open: clr
  and and_1 (and_1_out, Write_Enable, _2_en);
  Register #(.width(32)) _4 (.D(_4_in), .en(and_2_out), .Q(_4_out), .clk(Clock));  // open: clr
  and and_2 (and_2_out, Write_Enable, _4_en);
  Register #(.width(32)) _6 (.D(_6_in), .en(and_3_out), .Q(_6_out), .clk(Clock));  // open: clr
  and and_3 (and_3_out, Write_Enable, _6_en);
  Register #(.width(32)) _8 (.D(_8_in), .en(and_4_out), .Q(_8_out), .clk(Clock));  // open: clr
  and and_4 (and_4_out, Write_Enable, _8_en);
  Register #(.width(32)) _10 (.D(_10_in), .en(and_5_out), .Q(_10_out), .clk(Clock));  // open: clr
  and and_5 (and_5_out, Write_Enable, _10_en);
  Register #(.width(32)) _12 (.D(_12_in), .en(and_6_out), .Q(_12_out), .clk(Clock));  // open: clr
  and and_6 (and_6_out, Write_Enable, _12_en);
  Register #(.width(32)) _14 (.D(_14_in), .en(and_7_out), .Q(_14_out), .clk(Clock));  // open: clr
  and and_7 (and_7_out, Write_Enable, _14_en);
  Register #(.width(32)) _1 (.D(_1_in), .en(and_8_out), .Q(_1_out), .clk(Clock));  // open: clr
  and and_8 (and_8_out, Write_Enable, _1_en);
  Register #(.width(32)) _3 (.D(_3_in), .en(and_9_out), .Q(_3_out), .clk(Clock));  // open: clr
  and and_9 (and_9_out, Write_Enable, _3_en);
  Register #(.width(32)) _5 (.D(_5_in), .en(and_10_out), .Q(_5_out), .clk(Clock));  // open: clr
  and and_10 (and_10_out, Write_Enable, _5_en);
  Register #(.width(32)) _7 (.D(_7_in), .en(and_11_out), .Q(_7_out), .clk(Clock));  // open: clr
  and and_11 (and_11_out, Write_Enable, _7_en);
  Register #(.width(32)) _9 (.D(_9_in), .en(and_12_out), .Q(_9_out), .clk(Clock));  // open: clr
  and and_12 (and_12_out, Write_Enable, _9_en);
  Register #(.width(32)) _11 (.D(_11_in), .en(and_13_out), .Q(_11_out), .clk(Clock));  // open: clr
  and and_13 (and_13_out, Write_Enable, _11_en);
  Register #(.width(32)) _13 (.D(_13_in), .en(and_14_out), .Q(_13_out), .clk(Clock));  // open: clr
  and and_14 (and_14_out, Write_Enable, _13_en);
  Register #(.width(32)) _15 (.D(_15_in), .en(and_15_out), .Q(_15_out), .clk(Clock));  // open: clr
  and and_15 (and_15_out, Write_Enable, _15_en);
  Decoder #(.select(5)) decoder_1 (
    .out0(_0_en), .out1(_1_en), .out2(_2_en), .out3(_3_en), .out4(_4_en), .out5(_5_en), .out6(_6_en),
    .out7(_7_en), .out8(_8_en), .out9(_9_en), .out10(_10_en), .out11(_11_en), .out12(_12_en), .out13(_13_en),
    .out14(_14_en), .out15(_15_en), .out16(_16_en), .out17(_17_en), .out18(_18_en), .out19(_19_en),
    .out20(_20_en), .out21(_21en), .out22(_22_en), .out23(_23_en), .out24(_24_en), .out25(_25_en),
    .out26(_26_en), .out27(_27_en), .out28(_28_en), .out29(_29_en), .out30(_30_en), .out31(_31_en),
    .sel(Write_Register));  // open: en
  Register #(.width(32)) _16 (.D(_16_in), .en(and_16_out), .Q(s0_Value), .clk(Clock));  // open: clr
  and and_16 (and_16_out, Write_Enable, _16_en);
  Register #(.width(32)) _18 (.D(_18_in), .en(and_17_out), .Q(s2_Value), .clk(Clock));  // open: clr
  and and_17 (and_17_out, Write_Enable, _18_en);
  Register #(.width(32)) _20 (.D(_20_in), .en(and_18_out), .Q(_20_out), .clk(Clock));  // open: clr
  and and_18 (and_18_out, Write_Enable, _20_en);
  Register #(.width(32)) _22 (.D(_22_in), .en(and_19_out), .Q(_22_out), .clk(Clock));  // open: clr
  and and_19 (and_19_out, Write_Enable, _22_en);
  Register #(.width(32)) _24 (.D(_24_in), .en(and_20_out), .Q(_24_out), .clk(Clock));  // open: clr
  and and_20 (and_20_out, Write_Enable, _24_en);
  Register #(.width(32)) _26 (.D(_26_in), .en(and_21_out), .Q(_26_out), .clk(Clock));  // open: clr
  and and_21 (and_21_out, Write_Enable, _26_en);
  Register #(.width(32)) _28 (.D(_28_in), .en(and_22_out), .Q(_28_out), .clk(Clock));  // open: clr
  and and_22 (and_22_out, Write_Enable, _28_en);
  Register #(.width(32)) _30 (.D(_30_in), .en(and_23_out), .Q(_30_out), .clk(Clock));  // open: clr
  and and_23 (and_23_out, Write_Enable, _30_en);
  Register #(.width(32)) _17 (.D(_17_in), .en(and_24_out), .Q(s1_Value), .clk(Clock));  // open: clr
  and and_24 (and_24_out, Write_Enable, _17_en);
  Register #(.width(32)) _19 (.D(_19_in), .en(and_25_out), .Q(_19_out), .clk(Clock));  // open: clr
  and and_25 (and_25_out, Write_Enable, _19_en);
  Register #(.width(32)) _21 (.D(_21_in), .en(and_26_out), .Q(_21_out), .clk(Clock));  // open: clr
  and and_26 (and_26_out, Write_Enable, _21en);
  Register #(.width(32)) _23 (.D(_23_in), .en(and_27_out), .Q(_23_out), .clk(Clock));  // open: clr
  and and_27 (and_27_out, Write_Enable, _23_en);
  Register #(.width(32)) _25 (.D(_25_in), .en(and_28_out), .Q(_25_out), .clk(Clock));  // open: clr
  and and_28 (and_28_out, Write_Enable, _25_en);
  Register #(.width(32)) _27 (.D(_27_in), .en(and_29_out), .Q(_27_out), .clk(Clock));  // open: clr
  and and_29 (and_29_out, Write_Enable, _27_en);
  Register #(.width(32)) _29 (.D(_29_in), .en(and_30_out), .Q(sp_Value), .clk(Clock));  // open: clr
  and and_30 (and_30_out, Write_Enable, _29_en);
  Register #(.width(32)) _31 (.D(_31_in), .en(and_31_out), .Q(ra_Value), .clk(Clock));  // open: clr
  and and_31 (and_31_out, Write_Enable, _31_en);
  Multiplexer #(.select(5), .width(32), .enable("false")) multiplexer_1 (
    .in0(_0_out), .in1(_1_out), .in2(_2_out), .in3(_3_out), .in4(_4_out), .in5(_5_out), .in6(_6_out),
    .in7(_7_out), .in8(_8_out), .in9(_9_out), .in10(_10_out), .in11(_11_out), .in12(_12_out), .in13(_13_out),
    .in14(_14_out), .in15(_15_out), .in16(s0_Value), .in17(s1_Value), .in18(s2_Value), .in19(_19_out),
    .in20(_20_out), .in21(_21_out), .in22(_22_out), .in23(_23_out), .in24(_24_out), .in25(_25_out),
    .in26(_26_out), .in27(_27_out), .in28(_28_out), .in29(sp_Value), .in30(_30_out), .in31(ra_Value),
    .out(Read_Data_1), .sel(Read_Register_1));
  Multiplexer #(.select(5), .width(32), .enable("false")) multiplexer_2 (
    .in0(_0_out), .in1(_1_out), .in2(_2_out), .in3(_3_out), .in4(_4_out), .in5(_5_out), .in6(_6_out),
    .in7(_7_out), .in8(_8_out), .in9(_9_out), .in10(_10_out), .in11(_11_out), .in12(_12_out), .in13(_13_out),
    .in14(_14_out), .in15(_15_out), .in16(s0_Value), .in17(s1_Value), .in18(s2_Value), .in19(_19_out),
    .in20(_20_out), .in21(_21_out), .in22(_22_out), .in23(_23_out), .in24(_24_out), .in25(_25_out),
    .in26(_26_out), .in27(_27_out), .in28(_28_out), .in29(sp_Value), .in30(_30_out), .in31(ra_Value),
    .out(Read_Data_2), .sel(Read_Register_2));

  // Other names for the same wires on the sheet: _16_out[31:0] = s0_Value; _17_out[31:0] = s1_Value;
  //   _18_out[31:0] = s2_Value; _29_out[31:0] = sp_Value; _31_out[31:0] = ra_Value; clk = Clock;
  //   read_data1[31:0] = Read_Data_1; read_data2[31:0] = Read_Data_2; read_reg1[4:0] = Read_Register_1;
  //   read_reg2[4:0] = Read_Register_2; write_en = Write_Enable; write_reg[4:0] = Write_Register

  // Notes on the sheet:
  //   INPUTS to your circuit
  //   DON'T CHANGE THE LOCATIONS OF THE INPUTS AND OUTPUTS!
  //   These are DEBUG/TEST outputs from your circuit.
  //   OUTPUTS from your circuit
endmodule
