// Logisim project lab6ALU.circ as structural Verilog: 7 circuits, main circuit ALU
// LAB12-ALU
module ALU (
  input  [31:0] ALU_Source_1,
  input  [31:0] ALU_Source_2,
  input  [2:0] ALU_Control,
  output [31:0] ALU_Result
);

  wire [4:0] bit_extender_1_out;
  wire [31:0] AND, EXC_OR, INC_OR, RL, RR, SLL, SRA, SRL;

  // Probe on ALU_Source_1
  // Probe on ALU_Source_2
  Shifter #(.width(32)) shifter_1 (.in(ALU_Source_1), .\dist (bit_extender_1_out), .out(SLL));
  Bit_Extender #(.in_width(32), .out_width(5)) bit_extender_1 (.in(ALU_Source_2), .out(bit_extender_1_out));
  Shifter #(.width(32), .shift("rr")) shifter_2 (.in(ALU_Source_1), .\dist (bit_extender_1_out), .out(RR));
  Shifter #(.width(32), .shift("rl")) shifter_3 (.in(ALU_Source_1), .\dist (bit_extender_1_out), .out(RL));
  assign EXC_OR = ALU_Source_1 ^ ALU_Source_2;  // XOR_Gate xor_1, 32 bits wide
  Shifter #(.width(32), .shift("lr")) shifter_4 (.in(ALU_Source_1), .\dist (bit_extender_1_out), .out(SRL));
  Shifter #(.width(32), .shift("ar")) shifter_5 (.in(ALU_Source_1), .\dist (bit_extender_1_out), .out(SRA));
  assign AND = ALU_Source_1 & ALU_Source_2;  // AND_Gate and_1, 32 bits wide
  assign INC_OR = ALU_Source_1 | ALU_Source_2;  // OR_Gate or_1, 32 bits wide
  // Probe on ALU_Result
  Multiplexer #(.select(3), .width(32)) multiplexer_1 (
    .in0(SLL), .in1(SRL), .in2(SRA), .in3(RL), .in4(RR), .in5(AND), .in6(INC_OR), .in7(EXC_OR),
    .out(ALU_Result), .sel(ALU_Control));  // open: en

  // Other names for the same wires on the sheet: control[2:0] = ALU_Control; result[31:0] = ALU_Result;
  //   source1[31:0] = ALU_Source_1; source2[31:0] = ALU_Source_2

  // Notes on the sheet:
  //   DO NOT CROSS WIRES
  //   OVER THIS BOX
  //   DO NOT CROSS WIRES
  //   OVER THIS BOX
  //   COMPUTE ALL POSSIBLE OPERATIONS
  //   DO NOT CROSS WIRES
  //   OVER THIS BOX
  //   DO NOT CROSS WIRES
  //   OVER THIS BOX
  //   SELECT THE REQUESTED RESULT
  //   * YOUR CIRCUIT HERE *
  //   DO NOT CROSS WIRES
  //   OVER THIS BOX
endmodule

module Ex1 (
  input  [7:0] In_1,
  output Out_1,
  output [7:0] Out_2
);

  not not_1 (Out_2[7], In_1[7]);
  and and_1 (Out_1, In_1[0], In_1[7]);

  assign Out_2[6:0] = In_1[6:0];

  // Other names for the same wires on the sheet: Route_1[5:0] = In_1[6:1]
endmodule

module rotr (
  input  [3:0] Shift,
  input  [15:0] Number,
  output [15:0] out_3
);

  wire [15:0] n1_bit_1_out_2, n1_bit_2_out_2, n1_bit_3_out_2, n1_bit_4_out_2, n1_bit_5_out_2, n1_bit_6_out_2,
       n1_bit_7_out_2, n1_bit_8_out_2, n2_bit_1_out_2, n2_bit_2_out_2, n2_bit_3_out_2, n2_bit_4_out_2,
       n4_bit_1_out_2, n4_bit_2_out_2, n8_bit_1_out_2;

  _8_bit u_8_bit_1 (.Source_1(Number), .out_2(n8_bit_1_out_2));
  _4_bit u_4_bit_1 (.Source_1(n8_bit_1_out_2), .out_2(n4_bit_1_out_2));
  _2_bit u_2_bit_1 (.Source_1(n4_bit_1_out_2), .out_2(n2_bit_1_out_2));
  _1_bit u_1_bit_1 (.Source_1(n2_bit_1_out_2), .out_2(n1_bit_1_out_2));
  _1_bit u_1_bit_2 (.Source_1(n8_bit_1_out_2), .out_2(n1_bit_2_out_2));
  _2_bit u_2_bit_2 (.Source_1(n8_bit_1_out_2), .out_2(n2_bit_2_out_2));
  _1_bit u_1_bit_3 (.Source_1(n2_bit_2_out_2), .out_2(n1_bit_3_out_2));
  _1_bit u_1_bit_4 (.Source_1(n4_bit_1_out_2), .out_2(n1_bit_4_out_2));
  _4_bit u_4_bit_2 (.Source_1(Number), .out_2(n4_bit_2_out_2));
  _2_bit u_2_bit_3 (.Source_1(Number), .out_2(n2_bit_3_out_2));
  _2_bit u_2_bit_4 (.Source_1(n4_bit_2_out_2), .out_2(n2_bit_4_out_2));
  _1_bit u_1_bit_5 (.Source_1(n2_bit_4_out_2), .out_2(n1_bit_5_out_2));
  _1_bit u_1_bit_6 (.Source_1(n4_bit_2_out_2), .out_2(n1_bit_6_out_2));
  _1_bit u_1_bit_7 (.Source_1(Number), .out_2(n1_bit_7_out_2));
  _1_bit u_1_bit_8 (.Source_1(n2_bit_3_out_2), .out_2(n1_bit_8_out_2));
  Multiplexer #(.select(4), .width(16)) multiplexer_1 (
    .in0(Number), .in1(n1_bit_7_out_2), .in2(n2_bit_3_out_2), .in3(n1_bit_8_out_2), .in4(n4_bit_2_out_2),
    .in5(n1_bit_6_out_2), .in6(n2_bit_4_out_2), .in7(n1_bit_5_out_2), .in8(n8_bit_1_out_2),
    .in9(n1_bit_2_out_2), .in10(n2_bit_2_out_2), .in11(n1_bit_3_out_2), .in12(n4_bit_1_out_2),
    .in13(n1_bit_4_out_2), .in14(n2_bit_1_out_2), .in15(n1_bit_1_out_2), .out(out_3), .sel(Shift));  // open: en
endmodule

module _4_bit (
  input  [15:0] Source_1,
  output [15:0] out_2
);


  assign out_2 = {Source_1[3:0], Source_1[15:4]};
endmodule

module _2_bit (
  input  [15:0] Source_1,
  output [15:0] out_2
);


  assign out_2 = {Source_1[1:0], Source_1[15:2]};
endmodule

module _1_bit (
  input  [15:0] Source_1,
  output [15:0] out_2
);


  assign out_2 = {Source_1[0], Source_1[15:1]};
endmodule

module _8_bit (
  input  [15:0] Source_1,
  output [15:0] out_2
);


  assign out_2 = {Source_1[7:0], Source_1[15:8]};
endmodule
